# Fritzing sketch schem (saved by Fritzing 0.9.5d)

parts:
  Компонент1 = Arduino Nano (Rev3.0)
  M1 = Getriebemotor
  M2 = Getriebemotor
  Компонент2 = Motor Driver 1A Dual TB6612FNG
  Bat1 = battery_holder_single_18650
  S1 = Pushbutton [package="[THT]"]  # not connected
  S2 = Pololu QTR-8 Reflectabce Sensor array [package=THT]

nets:
  GND: Компонент1.GND, Компонент2.GND, Bat1.+#0, S2.pin1, S2.pin15
  N1: Компонент1.D6, M2.pin_2, Компонент2.B01
  N2: Компонент1.D7, Компонент2.STBY
  N3: Компонент1.D8, Компонент2.PWMB
  N4: Компонент1.D9, Компонент2.PWMA
  N5: Компонент1.D10, Компонент2.BIN1
  N6: Компонент1.D11/MOSI, Компонент2.BIN2
  N7: Компонент1.D12/MISO, Компонент2.AIN1
  5V: Компонент1.5V, Компонент2.VCC, S2.pin2, S2.pin14
  N8: Компонент1.A7, S2.pin5
  N9: Компонент1.A6, S2.pin6
  N10: Компонент1.A5, S2.pin7
  N11: Компонент1.A4, S2.pin8
  N12: Компонент1.A3, S2.pin9
  N13: Компонент1.A2, S2.pin10
  N14: Компонент1.A1, S2.pin11
  N15: Компонент1.A0, S2.pin12
  N16: Компонент1.D13/SCK, Компонент2.AIN2
  N17: M1.pin_1, Компонент2.A01
  N18: M1.pin_2, Компонент2.A02
  N19: M2.pin_1, Компонент2.B02
  N20: Компонент2.VM, Bat1.+#1

custom parts:
  battery_holder_single_18650: single 18650 battery holder
